// Logisim project SelectionSortQuasePronto.circ as structural Verilog: 6 circuits, main circuit main
module main (
  input  [7:0] data,
  input  data_av,
  output [3:0] Current_State,
  output done
);

  wire button_1_out, clk_out, not_1_out, selection_sort_1_ld, selection_sort_1_sel;
  wire [7:0] multiplexer_1_out, ram_1_data, selection_sort_1_address, selection_sort_1_data_out;

  // Probe on data
  Button button_1 (.out(button_1_out));
  Clock clk (.out(clk_out));
  // Probe on Current_State
  Multiplexer #(.width(8), .enable("false")) multiplexer_1 (
    .in0({8{1'b0}}), .in1(ram_1_data), .out(multiplexer_1_out), .sel(selection_sort_1_sel));
  Selection_Sort selection_sort_1 (
    .data_in(multiplexer_1_out), .data(data), .done(done), .clk(clk_out), .data_av(data_av),
    .rst(button_1_out), .data_out(selection_sort_1_data_out), .address(selection_sort_1_address),
    .sel(selection_sort_1_sel), .ld(selection_sort_1_ld), .Current_State(Current_State));
  not not_1 (not_1_out, selection_sort_1_ld);
  RAM ram_1 (
    .addr(selection_sort_1_address), .data(ram_1_data), .sel(selection_sort_1_sel), .clk(clk_out),
    .ld(not_1_out));  // open: clr
  assign ram_1_data = selection_sort_1_ld ? selection_sort_1_data_out : 8'bz;  // Controlled_Buffer controlled_buffer_1
endmodule

module Selection_Sort (
  input  [7:0] data_in,
  input  [7:0] data,
  input  clk,
  input  data_av,
  input  rst,
  output [7:0] data_out,
  output [7:0] address,
  output sel,
  output done,
  output [3:0] Current_State,
  output ld
);

  wire control_path_1_seladdr0, control_path_1_seladdr1, control_path_1_selcomp, control_path_1_seldata_out,
       control_path_1_seli1, control_path_1_selinc, control_path_1_selmin, control_path_1_selmuxaux,
       control_path_1_wraux, control_path_1_wri, control_path_1_wrj, control_path_1_wrmin,
       control_path_1_wrorder, control_path_1_wrsize, control_path_1_wrstartaddr, datapath_1_aux_t_min,
       datapath_1_i_dt_min, datapath_1_lt_size;

  Control_Path control_path_1 (
    .data_av(data_av), .lt_size(datapath_1_lt_size), .i_dt_min(datapath_1_i_dt_min),
    .aux_t_min(datapath_1_aux_t_min), .clk(clk), .rst(rst), .Current_State(Current_State),
    .wrStartAddr(control_path_1_wrstartaddr), .wrI(control_path_1_wri), .wrSize(control_path_1_wrsize),
    .seli1(control_path_1_seli1), .wrJ(control_path_1_wrj), .wrOrder(control_path_1_wrorder),
    .selData_Out(control_path_1_seldata_out), .selInc(control_path_1_selinc), .done(done),
    .selComp(control_path_1_selcomp), .selMin(control_path_1_selmin), .wrMin(control_path_1_wrmin),
    .selAddr0(control_path_1_seladdr0), .selAddr1(control_path_1_seladdr1),
    .selMuxAux(control_path_1_selmuxaux), .wrAux(control_path_1_wraux), .sel(sel), .ld(ld));
  DataPath datapath_1 (
    .data_in(data_in), .data(data), .rst(rst), .clk(clk), .data_out(data_out),
    .aux_t_min(datapath_1_aux_t_min), .address(address), .i_dt_min(datapath_1_i_dt_min),
    .lt_size(datapath_1_lt_size), .wrOrder(control_path_1_wrorder), .wrStartAddr(control_path_1_wrstartaddr),
    .wrSize(control_path_1_wrsize), .seli1(control_path_1_seli1), .wrI(control_path_1_wri),
    .wrJ(control_path_1_wrj), .selMuxAux(control_path_1_selmuxaux), .wrAux(control_path_1_wraux),
    .selMin(control_path_1_selmin), .selInc(control_path_1_selinc), .wrMin(control_path_1_wrmin),
    .selComp(control_path_1_selcomp), .selAddr0(control_path_1_seladdr0),
    .selData_out(control_path_1_seldata_out), .selAddr1(control_path_1_seladdr1));  // open: wrAux2
endmodule

module DataPath (
  input  wrAux2,
  input  selData_out,
  input  wrAux,
  input  selMuxAux,
  input  [7:0] data_in,
  input  wrMin,
  input  selMin,
  input  selAddr1,
  input  wrOrder,
  input  selAddr0,
  input  wrI,
  input  seli1,
  input  selInc,
  input  wrStartAddr,
  input  [7:0] data,
  input  selComp,
  input  wrJ,
  input  wrSize,
  input  rst,
  input  clk,
  output [7:0] data_out,
  output aux_t_min,
  output [7:0] address,
  output i_dt_min,
  output lt_size
);

  wire comparator_1_gt, comparator_1_lt, comparator_2_eq;
  wire [6:0] subtractor_1_out;
  wire [7:0] adder_1_out, and_1_out, multiplexer_1_out, multiplexer_2_out, multiplexer_3_out,
       multiplexer_4_out, multiplexer_6_out, multiplexer_7_out, reg_aux2_q, reg_aux_q, reg_i_q, reg_J_q,
       reg_min_q, reg_order_q, reg_size_q, reg_startAddr_q, xor_1_out, xor_2_out;

  // Probe on data
  Register reg_order (.D(data), .en(wrOrder), .Q(reg_order_q), .clk(clk), .clr(rst));
  Register reg_startAddr (.D(data), .en(wrStartAddr), .Q(reg_startAddr_q), .clk(clk), .clr(rst));
  Register reg_size (.D(data), .en(wrSize), .Q(reg_size_q), .clk(clk), .clr(rst));
  assign and_1_out = 8'h1 & reg_order_q;  // AND_Gate and_1, 8 bits wide
  // Probe on data_in
  Multiplexer #(.width(8), .disabled(0), .enable("false")) multiplexer_1 (
    .in0(adder_1_out), .in1(reg_startAddr_q), .out(multiplexer_1_out), .sel(seli1));
  Register reg_i (.D(multiplexer_1_out), .en(wrI), .Q(reg_i_q), .clk(clk), .clr(rst));
  Register reg_J (.D(adder_1_out), .en(wrJ), .Q(reg_J_q), .clk(clk), .clr(rst));
  // Probe on xor_1_out
  Multiplexer #(.width(8), .enable("false")) multiplexer_2 (
    .in0(xor_1_out), .in1(data_in), .out(multiplexer_2_out), .sel(selMuxAux));
  Register reg_aux (.D(multiplexer_2_out), .en(wrAux), .Q(reg_aux_q), .clk(clk), .clr(rst));
  Multiplexer #(.width(8), .enable("false")) multiplexer_3 (
    .in0(reg_i_q), .in1(reg_J_q), .out(multiplexer_3_out), .sel(selMin));
  Multiplexer #(.width(8), .disabled(0), .enable("false")) multiplexer_4 (
    .in0(reg_i_q), .in1(reg_J_q), .out(multiplexer_4_out), .sel(selInc));
  assign xor_1_out = reg_aux_q ^ reg_aux2_q;  // XOR_Gate xor_1, 8 bits wide
  Register reg_aux2 (.D(xor_2_out), .en(wrAux2), .Q(reg_aux2_q), .clk(clk), .clr(rst));
  Register reg_min (.D(multiplexer_3_out), .en(wrMin), .Q(reg_min_q), .clk(clk), .clr(rst));
  Adder adder_1 (.a(multiplexer_4_out), .b(8'h1), .out(adder_1_out));  // open: cin, cout
  // Probe on xor_2_out
  assign xor_2_out = data_in ^ reg_aux_q;  // XOR_Gate xor_2, 8 bits wide
  Comparator comparator_1 (.a(reg_aux_q), .b(data_in), .gt(comparator_1_gt), .lt(comparator_1_lt));  // open: eq
  Multiplexer #(.enable("false")) multiplexer_5 (
    .in0(comparator_1_gt), .in1(comparator_1_lt), .out(aux_t_min), .sel(and_1_out[0]));
  Multiplexer #(.width(8), .enable("false")) multiplexer_6 (
    .in0(reg_J_q), .in1(reg_i_q), .out(multiplexer_6_out), .sel(selAddr0));
  Comparator comparator_2 (.a(reg_min_q), .b(reg_i_q), .eq(comparator_2_eq));  // open: gt, lt
  not not_1 (i_dt_min, comparator_2_eq);
  // Probe on multiplexer_7_out
  Multiplexer #(.width(8), .disabled(0), .enable("false")) multiplexer_7 (
    .in0(adder_1_out), .in1(reg_J_q), .out(multiplexer_7_out), .sel(selComp));
  Multiplexer #(.width(8), .disabled(0), .enable("false")) multiplexer_8 (
    .in0(reg_aux2_q), .in1(reg_aux_q), .out(data_out), .sel(selData_out));
  Multiplexer #(.width(8), .enable("false")) multiplexer_9 (
    .in0(reg_min_q), .in1(multiplexer_6_out), .out(address), .sel(selAddr1));
  Subtractor subtractor_1 (
    .a(multiplexer_7_out), .b(reg_size_q), .out({lt_size, subtractor_1_out}));  // open: bin, bout
  // Probe on data_out

  // Notes on the sheet:
  //   ld StartAddr
  //   i++
  //   xor
  //   data_in
  //   || i++
  //   j++
  //   i
  //   j
  //   i++
  //   j++
  //   aux
  //   aux2
  //   aux
  //   mem[min]
  //   order == 0 >
  //   order == 1 <
  //   i + 1 < size
  //   j < size
  //   xor
  //   aux
  //   j
  //   i
  //   min
endmodule

module Control_Path (
  input  data_av,
  input  lt_size,
  input  i_dt_min,
  input  aux_t_min,
  input  clk,
  input  rst,
  output wrStartAddr,
  output wrI,
  output wrSize,
  output seli1,
  output wrJ,
  output wrOrder,
  output selData_Out,
  output [3:0] Current_State,
  output selInc,
  output done,
  output selComp,
  output selMin,
  output wrMin,
  output selAddr0,
  output selAddr1,
  output selMuxAux,
  output wrAux,
  output sel,
  output ld
);

  wire [3:0] nextstate_1_d0;

  NextState nextstate_1 (
    .Q3(Current_State[3]), .Q2(Current_State[2]), .Q1(Current_State[1]), .Q0(Current_State[0]),
    .data_av(data_av), .lt_size(lt_size), .i_dt_min(i_dt_min), .aux_t_min(aux_t_min), .D3(nextstate_1_d0[3]),
    .D2(nextstate_1_d0[2]), .D1(nextstate_1_d0[1]), .D0(nextstate_1_d0[0]));
  Register #(.width(4)) register_1 (.D(nextstate_1_d0), .Q(Current_State), .clk(clk), .clr(rst));  // open: en
  Output output_1 (
    .Q3(Current_State[3]), .Q2(Current_State[2]), .Q1(Current_State[1]), .Q0(Current_State[0]),
    .wrStartAddr(wrStartAddr), .wrI(wrI), .wrSize(wrSize), .seli1(seli1), .wrJ(wrJ), .wrOrder(wrOrder),
    .selData_out(selData_Out), .selInc(selInc), .done(done), .selComp(selComp), .done_2(selMin),
    .selMin(wrMin), .wrMin(selAddr0), .selAddr0(selAddr1), .selAddr1(selMuxAux), .selMuxAux(wrAux),
    .wrAux(sel), .sel(ld));  // open: ld
endmodule

module NextState (
  input  Q3,
  input  Q2,
  input  Q1,
  input  Q0,
  input  data_av,
  input  lt_size,
  input  i_dt_min,
  input  aux_t_min,
  output D3,
  output D2,
  output D1,
  output D0
);

  wire and_1_out, and_2_out, and_3_out, and_4_out, and_5_out, and_6_out, and_7_out, and_8_out, and_9_out,
       and_10_out, and_11_out, and_12_out, and_13_out, and_14_out, and_15_out, and_16_out, and_17_out,
       and_18_out, and_19_out, and_20_out, and_21_out, and_22_out, and_23_out, and_24_out, and_25_out,
       and_26_out, and_27_out, and_28_out, not_1_out, not_2_out, not_3_out, not_4_out, not_5_out, not_6_out,
       not_7_out, not_8_out, not_9_out, not_10_out, not_11_out, not_12_out, not_13_out, not_14_out,
       not_15_out, not_16_out, not_17_out, not_18_out, not_19_out, not_20_out, not_21_out, not_22_out,
       not_23_out, not_24_out, not_25_out, not_26_out, not_27_out, not_28_out, not_29_out, not_30_out,
       not_31_out, not_32_out, not_33_out, not_34_out, not_35_out, not_36_out, not_37_out, not_38_out,
       not_39_out, not_40_out, not_41_out, not_42_out, not_43_out, not_44_out, not_45_out, not_46_out,
       not_47_out, not_48_out, not_49_out, not_50_out;

  not not_1 (not_1_out, Q2);
  not not_2 (not_2_out, lt_size);
  not not_3 (not_3_out, Q3);
  not not_4 (not_4_out, lt_size);
  not not_5 (not_5_out, Q3);
  not not_6 (not_6_out, aux_t_min);
  not not_7 (not_7_out, Q3);
  not not_8 (not_8_out, Q2);
  not not_9 (not_9_out, Q1);
  not not_10 (not_10_out, Q0);
  not not_11 (not_11_out, Q2);
  not not_12 (not_12_out, Q1);
  not not_13 (not_13_out, Q0);
  not not_14 (not_14_out, Q3);
  not not_15 (not_15_out, Q0);
  not not_16 (not_16_out, Q1);
  not not_17 (not_17_out, Q1);
  not not_18 (not_18_out, Q0);
  not not_19 (not_19_out, Q1);
  not not_20 (not_20_out, Q2);
  not not_21 (not_21_out, Q1);
  not not_22 (not_22_out, Q3);
  not not_23 (not_23_out, Q2);
  not not_24 (not_24_out, lt_size);
  not not_25 (not_25_out, Q2);
  not not_26 (not_26_out, Q0);
  not not_27 (not_27_out, Q0);
  not not_28 (not_28_out, Q1);
  not not_29 (not_29_out, Q1);
  not not_30 (not_30_out, Q0);
  not not_31 (not_31_out, Q2);
  not not_32 (not_32_out, Q0);
  not not_33 (not_33_out, Q3);
  not not_34 (not_34_out, Q2);
  not not_35 (not_35_out, Q1);
  not not_36 (not_36_out, data_av);
  not not_37 (not_37_out, Q3);
  not not_38 (not_38_out, Q2);
  not not_39 (not_39_out, lt_size);
  not not_40 (not_40_out, Q3);
  not not_41 (not_41_out, Q1);
  not not_42 (not_42_out, lt_size);
  not not_43 (not_43_out, Q1);
  not not_44 (not_44_out, Q0);
  not not_45 (not_45_out, Q3);
  not not_46 (not_46_out, Q0);
  not not_47 (not_47_out, Q2);
  not not_48 (not_48_out, Q0);
  not not_49 (not_49_out, Q2);
  not not_50 (not_50_out, Q1);
  and and_1 (and_1_out, not_1_out, Q1, Q0, not_2_out);
  and and_2 (and_2_out, not_3_out, Q2, Q0, not_4_out);
  and and_3 (and_3_out, not_5_out, Q2, Q1, not_6_out);
  and and_4 (and_4_out, not_7_out, Q2, Q1, Q0);
  and and_5 (and_5_out, Q3, not_8_out, Q0);
  and and_6 (and_6_out, Q3, Q2, not_9_out);
  and and_7 (and_7_out, Q3, Q2, not_10_out);
  and and_8 (and_8_out, not_11_out, Q1, Q0);
  and and_9 (and_9_out, Q2, not_12_out, not_13_out);
  and and_10 (and_10_out, not_14_out, Q2, not_15_out, aux_t_min);
  and and_11 (and_11_out, Q2, not_16_out, lt_size);
  and and_12 (and_12_out, Q3, not_17_out, not_18_out);
  and and_13 (and_13_out, Q3, Q2, not_19_out);
  and and_14 (and_14_out, not_20_out, not_21_out, Q0, data_av);
  and and_15 (and_15_out, not_22_out, not_23_out, Q1, not_24_out);
  and and_16 (and_16_out, not_25_out, Q1, not_26_out);
  and and_17 (and_17_out, Q1, not_27_out, aux_t_min);
  and and_18 (and_18_out, Q2, not_28_out, Q0, lt_size);
  and and_19 (and_19_out, Q3, not_29_out, Q0);
  and and_20 (and_20_out, Q3, Q1, not_30_out);
  and and_21 (and_21_out, not_31_out, not_32_out, data_av);
  and and_22 (and_22_out, not_33_out, not_34_out, not_35_out, Q0, not_36_out);
  and and_23 (and_23_out, not_37_out, not_38_out, Q1, Q0, not_39_out);
  and and_24 (and_24_out, not_40_out, Q2, not_41_out, not_42_out);
  and and_25 (and_25_out, Q2, not_43_out, not_44_out);
  and and_26 (and_26_out, not_45_out, Q2, not_46_out, aux_t_min);
  and and_27 (and_27_out, Q3, not_47_out, not_48_out);
  and and_28 (and_28_out, Q3, not_49_out, not_50_out, i_dt_min);
  or or_1 (D3, and_1_out, and_2_out, and_3_out, and_4_out, and_5_out, and_6_out, and_7_out);
  or or_2 (D2, and_8_out, and_9_out, and_10_out, and_11_out, and_12_out, and_13_out);
  or or_3 (D1, and_14_out, and_15_out, and_16_out, and_17_out, and_18_out, and_19_out, and_20_out);
  or or_4 (D0, and_21_out, and_22_out, and_23_out, and_24_out, and_25_out, and_26_out, and_27_out, and_28_out);
endmodule

module Output (
  input  Q3,
  input  Q2,
  input  Q1,
  input  Q0,
  output wrStartAddr,
  output wrI,
  output wrSize,
  output seli1,
  output wrJ,
  output wrOrder,
  output selData_out,
  output selInc,
  output done,
  output selComp,
  output done_2,
  output selMin,
  output wrMin,
  output selAddr0,
  output selAddr1,
  output selMuxAux,
  output wrAux,
  output sel,
  output ld
);

  wire and_1_out, and_2_out, and_3_out, and_4_out, and_9_out, and_10_out, and_11_out, and_12_out, and_13_out,
       and_14_out, and_15_out, and_16_out, and_17_out, and_18_out, and_19_out, and_20_out, and_21_out,
       and_22_out, not_1_out, not_2_out, not_3_out, not_4_out, not_5_out, not_6_out, not_7_out, not_8_out,
       not_9_out, not_10_out, not_11_out, not_12_out, not_13_out, not_14_out, not_15_out, not_16_out,
       not_17_out, not_18_out, not_19_out, not_20_out, not_21_out, not_22_out, not_23_out, not_24_out,
       not_25_out, not_26_out, not_27_out, not_28_out, not_29_out, not_30_out, not_31_out, not_32_out,
       not_33_out, not_34_out, not_35_out, not_36_out, not_37_out, not_38_out, not_39_out, not_40_out,
       not_41_out, not_42_out, not_43_out, not_44_out, not_45_out, not_46_out, not_47_out, not_48_out,
       not_49_out, not_50_out, not_51_out, not_52_out, not_53_out;

  not not_1 (not_1_out, Q3);
  not not_2 (not_2_out, Q2);
  not not_3 (not_3_out, Q2);
  not not_4 (not_4_out, Q0);
  not not_5 (not_5_out, Q3);
  not not_6 (not_6_out, Q0);
  not not_7 (not_7_out, Q0);
  not not_8 (not_8_out, Q2);
  not not_9 (not_9_out, Q0);
  not not_10 (not_10_out, Q0);
  not not_11 (not_11_out, Q2);
  not not_12 (not_12_out, Q0);
  not not_13 (not_13_out, Q0);
  not not_14 (not_14_out, Q3);
  not not_15 (not_15_out, Q0);
  not not_16 (not_16_out, Q3);
  not not_17 (not_17_out, Q3);
  not not_18 (not_18_out, Q3);
  not not_19 (not_19_out, Q0);
  not not_20 (not_20_out, Q2);
  not not_21 (not_21_out, Q0);
  not not_22 (not_22_out, Q0);
  not not_23 (not_23_out, Q3);
  not not_24 (not_24_out, Q0);
  not not_25 (not_25_out, Q2);
  not not_26 (not_26_out, Q0);
  not not_27 (not_27_out, Q0);
  not not_28 (not_28_out, Q3);
  not not_29 (not_29_out, Q0);
  not not_30 (not_30_out, Q2);
  not not_31 (not_31_out, Q0);
  not not_32 (not_32_out, Q0);
  not not_33 (not_33_out, Q2);
  not not_34 (not_34_out, Q0);
  not not_35 (not_35_out, Q0);
  not not_36 (not_36_out, Q2);
  not not_37 (not_37_out, Q0);
  not not_38 (not_38_out, Q0);
  and and_1 (and_1_out, not_1_out, not_2_out, Q0);
  and and_2 (and_2_out, Q3, not_3_out, Q0, not_4_out);
  and and_3 (and_3_out, not_5_out, Q2, not_6_out, not_7_out);
  and and_4 (and_4_out, Q3, not_8_out, not_9_out, not_10_out);
  and and_5 (selInc, Q3, not_11_out, not_12_out, not_13_out);
  and and_6 (selComp, not_14_out, Q2, not_15_out, Q0);
  and and_7 (selMin, not_16_out, Q2, Q0, Q0);
  and and_8 (wrMin, not_17_out, Q2, Q0, Q0);
  and and_9 (and_9_out, not_18_out, Q2, not_19_out, Q0);
  and and_10 (and_10_out, Q3, not_20_out, not_21_out, Q0);
  and and_11 (and_11_out, Q3, Q2, Q0, not_22_out);
  and and_12 (and_12_out, not_23_out, Q2, not_24_out, Q0);
  and and_13 (and_13_out, Q3, not_25_out, not_26_out, Q0);
  and and_14 (and_14_out, Q3, Q2, Q0, not_27_out);
  and and_15 (and_15_out, not_28_out, Q2, not_29_out, Q0);
  and and_16 (and_16_out, Q3, not_30_out, not_31_out, Q0);
  and and_17 (and_17_out, Q2, not_32_out, Q0);
  or or_1 (wrAux, and_17_out, and_18_out);
  and and_18 (and_18_out, Q3, not_33_out, Q0);
  and and_19 (and_19_out, Q2, not_34_out, Q0);
  and and_20 (and_20_out, Q2, Q0, not_35_out);
  and and_21 (and_21_out, Q3, not_36_out, Q0);
  and and_22 (and_22_out, Q3, Q2, not_37_out);
  and and_23 (ld, Q3, Q2, not_38_out);
  or or_2 (wrI, and_1_out, and_2_out);
  or or_3 (wrJ, and_3_out, and_4_out);
  or or_4 (selAddr0, and_9_out, and_10_out, and_11_out);
  or or_5 (selAddr1, and_12_out, and_13_out, and_14_out);
  or or_6 (selMuxAux, and_15_out, and_16_out);
  or or_7 (sel, and_19_out, and_20_out, and_21_out, and_22_out);
  not not_39 (not_39_out, Q3);
  not not_40 (not_40_out, Q3);
  not not_41 (not_41_out, Q2);
  and and_24 (wrStartAddr, not_40_out, not_41_out, not_42_out, not_43_out);
  not not_42 (not_42_out, Q0);
  not not_43 (not_43_out, Q0);
  not not_44 (not_44_out, Q3);
  not not_45 (not_45_out, Q2);
  and and_25 (wrSize, not_44_out, not_45_out, not_46_out, Q0);
  not not_46 (not_46_out, Q0);
  not not_47 (not_47_out, Q3);
  not not_48 (not_48_out, Q2);
  and and_26 (seli1, not_47_out, not_48_out, not_49_out, Q0);
  not not_49 (not_49_out, Q0);
  not not_50 (not_50_out, Q3);
  not not_51 (not_51_out, Q2);
  and and_27 (wrOrder, not_50_out, not_51_out, Q0, not_52_out);
  not not_52 (not_52_out, Q0);
  and and_28 (selData_out, Q3, Q2, Q0, not_53_out);
  not not_53 (not_53_out, Q0);
  and and_29 (done, Q3, Q2, Q0, Q0);
  and and_30 (done_2, Q0, Q0, Q2, not_39_out);

  assign Q1 = Q0;

  // Notes on the sheet:
  //   Q3 Q2 Q1 Q0
endmodule
